# Fritzing sketch fidgetspinner (saved by Fritzing 0.9.1b)
circuit board: 5cm x 5cm
breadboards: 1

parts:
  VCC1 = Battery
  S1 = SWITCH-MOMENTARY-2 [package=reed_switch_plastic]
  L1 = Inductor [package="400 mil [THT]"]
  D1 = Diode [package=diode-1n4001]
  R1 = Resistor [tolerance=±5% resistance=220 package=THT]
  Q1 = Basic FET N-Channel [package="TO220 [THT]"]

nets:
  N1: VCC1.-, R1.Pin_0, Q1.source
  N2: VCC1.+, S1.2, L1.pin_1, D1.C
  N3: S1.1, R1.Pin_1, Q1.gate
  N4: L1.pin_0, D1.A, Q1.drain

notes:
  -
  +
  20th Anniversary
  Make & Take
